// Logisim project COProject.circ as structural Verilog: 2 circuits, main circuit main
module main (
);

  wire ACLOAD, alu_1_cout, and_1_out, and_2_out, and_3_out, and_4_out, and_5_out, and_6_out, and_7_out,
       and_8_out, and_9_out, and_10_out, and_11_out, and_14_out, and_15_out, and_16_out, and_17_out,
       and_18_out, and_19_out, and_20_out, and_21_out, and_22_out, and_23_out, and_24_out, and_25_out,
       and_26_out, and_27_out, and_28_out, and_29_out, and_30_out, and_31_out, and_32_out, and_33_out,
       and_34_out, and_35_out, and_36_out, and_37_out, and_38_out, and_39_out, and_40_out, and_41_out,
       and_42_out, and_43_out, and_44_out, and_45_out, and_46_out, and_47_out, and_48_out, and_49_out,
       and_50_out, and_51_out, and_52_out, and_53_out, and_54_out, and_55_out, ARLOAD, bitselector_1_out,
       CHECKIFZERO, CLEAR_out, clock_1_out, D0, D1, D2, D3, D4, D5, D6, D7, d_ff_1_q, DRINC, DRLOAD, E_q,
       I_q, or_3_out, or_6_out, or_7_out, or_8_out, or_9_out, or_10_out, or_11_out, PCINC, PCLOAD, READ, STR,
       T0, T1, T2, T3, T4, T5, T6, T7, TRLOAD;
  wire [2:0] bitselector_2_out, priority_encoder_1_out, priority_encoder_2_out;
  wire [3:0] SC_q;
  wire [6:0] AR_q, bit_extender_1_out, bit_extender_2_out, PC_q;
  wire [15:0] AC_q, alu_1_out, bit_extender_3_out, bit_extender_4_out, DR_q, IR, multiplexer_1_out,
       ram_1_data, TR_q;

  Decoder #(.select(4)) decoder_1 (
    .out0(T0), .out1(T1), .out2(T2), .out3(T3), .out4(T4), .out5(T5), .out6(T6), .out7(T7), .sel(SC_q));  // open: out8, out9, out10, out11, out12, out13, out14, out15, en
  Counter #(.width(4), .max('hf)) SC (
    .D(4'b0000), .count(1'b1), .Q(SC_q), .clk(clock_1_out), .clr(d_ff_1_q));  // open: load, carry
  BitSelector #(.width(16)) bitselector_1 (.in(IR), .out(bitselector_1_out), .sel(4'b1111));
  or CLEAR (CLEAR_out, and_8_out, and_7_out, and_6_out, and_5_out, and_4_out, and_3_out, and_2_out, and_1_out);
  BitSelector #(.width(16), .group(3)) bitselector_2 (.in(IR), .out(bitselector_2_out), .sel(3'b100));
  D_Flip_Flop I (.clk(clock_1_out), .D(bitselector_1_out), .Q(I_q));  // open: Qn, preset, en, reset
  D_Flip_Flop d_ff_1 (.clk(clock_1_out), .D(CLEAR_out), .Q(d_ff_1_q));  // open: Qn, preset, en, reset
  and and_1 (and_1_out, D6, T5);
  and and_2 (and_2_out, D2, T4);
  and and_3 (and_3_out, D0, T7);
  and and_4 (and_4_out, D1, T4);
  and and_5 (and_5_out, D3, T3);
  and and_6 (and_6_out, D2, T4);
  and and_7 (and_7_out, D5, T4);
  and and_8 (and_8_out, D4, T3);
  Decoder #(.select(3)) decoder_2 (
    .out0(D0), .out1(D1), .out2(D2), .out3(D3), .out4(D4), .out5(D5), .out6(D6), .out7(D7),
    .sel(bitselector_2_out));  // open: en
  and and_9 (and_9_out, and_11_out, CHECKIFZERO);
  and and_10 (and_10_out, T3, D0);
  or or_1 (PCINC, T1, and_9_out);
  and and_11 (and_11_out, D6, T5);
  buf or_2 (TRLOAD, and_10_out);  // OR_Gate
  and and_12 (PCLOAD, D4, T3);
  and and_13 (DRINC, D6, T4);
  or or_3 (or_3_out, and_15_out, and_14_out);
  and and_14 (and_14_out, D0, T5);
  and and_15 (and_15_out, D2, T4);
  and and_16 (and_16_out, D2, T3);
  and and_17 (and_17_out, T4, D0);
  and and_18 (and_18_out, T6, D0);
  and and_19 (and_19_out, T3, D1);
  and and_20 (and_20_out, T3, D2);
  and and_21 (and_21_out, T3, D6);
  and and_22 (and_22_out, T3, D3);
  alu alu_1 (.A(DR_q), .B(AC_q), .in_2(priority_encoder_1_out), .Cout(alu_1_cout), .out(alu_1_out));
  Priority_Encoder priority_encoder_1 (
    .in1(or_3_out), .in3(and_23_out), .in5(and_24_out), .in6(and_28_out), .out(priority_encoder_1_out));  // open: in0, in2, in4, in7, en_in
  and and_23 (and_23_out, D5, T4);
  and and_24 (and_24_out, D0, T7);
  and and_25 (and_25_out, T3, D5);
  or or_4 (DRLOAD, and_25_out, and_16_out, and_17_out, and_18_out, and_19_out, and_20_out, and_21_out);
  and and_26 (and_26_out, T5, D6);
  D_Flip_Flop E (.clk(clock_1_out), .D(alu_1_cout), .Q(E_q), .en(and_27_out));  // open: Qn, preset, reset
  and and_27 (and_27_out, T4, D1);
  and and_28 (and_28_out, D1, T4);
  or or_5 (STR, and_22_out, and_26_out);
  Clock clock_1 (.out(clock_1_out));
  and and_29 (and_29_out, D0, T6);
  and and_30 (and_30_out, T4, D0);
  and and_31 (and_31_out, D0, T3);
  and and_32 (and_32_out, D0, T5);
  and and_33 (and_33_out, D6, T5);
  Bit_Extender #(.in_width(16), .out_width(7)) bit_extender_1 (.in(multiplexer_1_out), .out(bit_extender_1_out));
  and and_34 (and_34_out, T4, D0);
  and and_35 (and_35_out, T3, D2);
  and and_36 (and_36_out, D3, T3);
  or or_6 (or_6_out, and_32_out, and_33_out);
  Bit_Extender #(.in_width(16), .out_width(7)) bit_extender_2 (.in(multiplexer_1_out), .out(bit_extender_2_out));
  and and_37 (and_37_out, T3, D2);
  or or_7 (or_7_out, and_31_out, and_36_out);
  Register #(.width(7)) AR (.D(bit_extender_2_out), .en(ARLOAD), .Q(AR_q), .clk(clock_1_out));  // open: clr
  Counter #(.width(7), .max('h7f)) PC (
    .load(PCLOAD), .D(bit_extender_1_out), .count(PCINC), .Q(PC_q), .clk(clock_1_out));  // open: carry, clr
  Register #(.width(16)) AC (.D(alu_1_out), .en(ACLOAD), .Q(AC_q), .clk(clock_1_out));  // open: clr
  Counter #(.width(16), .max('hffff)) DR (
    .load(DRLOAD), .D(multiplexer_1_out), .count(DRINC), .Q(DR_q), .clk(clock_1_out));  // open: carry, clr
  Register #(.width(16)) TR (.D(multiplexer_1_out), .en(TRLOAD), .Q(TR_q), .clk(clock_1_out));  // open: clr
  Register #(.width(16)) u_IR (.D(multiplexer_1_out), .en(T1), .Q(IR), .clk(clock_1_out));  // open: clr
  and and_38 (and_38_out, T3, D2);
  and and_39 (and_39_out, D5, T3);
  and and_40 (and_40_out, T3, D6);
  buf or_8 (or_8_out, and_29_out);  // OR_Gate
  assign bit_extender_3_out = {{9{1'b0}}, PC_q};  // Bit_Extender bit_extender_3
  and and_41 (and_41_out, D1, T3);
  or or_9 (or_9_out, and_39_out, and_38_out, T1, and_37_out, and_41_out, and_30_out, and_34_out, and_35_out, and_40_out);
  and and_42 (and_42_out, T3, D4);
  buf or_10 (or_10_out, T0);  // OR_Gate
  Priority_Encoder priority_encoder_2 (
    .in0(or_9_out), .in1(and_42_out), .in2(or_10_out), .in3(or_7_out), .in4(or_6_out), .in5(or_8_out),
    .in7(or_11_out), .out(priority_encoder_2_out));  // open: in6, en_in, gs, en_out
  buf or_11 (or_11_out, T2);  // OR_Gate
  RAM #(.addrWidth(7), .dataWidth(16), .bus("separate")) ram_1 (
    .addr(AR_q), .din(multiplexer_1_out), .data(ram_1_data), .str(STR), .clk(clock_1_out), .ld(READ));  // open: sel, clr
  assign bit_extender_4_out = {{9{1'b0}}, AR_q};  // Bit_Extender bit_extender_4
  Comparator #(.width(16)) comparator_1 (.a(DR_q), .b({16{1'b0}}), .eq(CHECKIFZERO));  // open: gt, lt
  and and_43 (and_43_out, T4, D2);
  and and_44 (and_44_out, T5, D0);
  and and_45 (and_45_out, T7, D0);
  and and_46 (and_46_out, T4, D1);
  and and_47 (and_47_out, T4, D2);
  Multiplexer #(.select(3), .width(16), .enable("false")) multiplexer_1 (
    .in0(ram_1_data), .in1(bit_extender_4_out), .in2(bit_extender_3_out), .in3(AC_q), .in4(DR_q), .in5(TR_q),
    .in7(IR), .out(multiplexer_1_out), .sel(priority_encoder_2_out));  // open: in6
  or or_12 (ARLOAD, T0, T2);
  and and_48 (and_48_out, T4, D5);
  and and_49 (and_49_out, T5, D5);
  or or_13 (ACLOAD, and_49_out, and_43_out, and_44_out, and_45_out, and_46_out, and_47_out, and_48_out);
  and and_50 (and_50_out, T4, D0);
  and and_51 (and_51_out, D1, T3);
  and and_52 (and_52_out, D2, T3);
  and and_53 (and_53_out, T3, D5);
  and and_54 (and_54_out, D2, T3);
  and and_55 (and_55_out, T3, D6);
  or or_14 (READ, and_54_out, and_50_out, and_51_out, T1, and_52_out, and_53_out, and_55_out);
endmodule

// ALU
module alu (
  input  [15:0] A,
  input  [2:0] in_2,
  input  [15:0] B,
  output Cout,
  output [15:0] out
);

  wire [15:0] adder_1_out, adder_2_out, divider_1_out, multiplier_1_out, subtractor_1_out, xor_1_out;

  Adder #(.width(16)) adder_1 (.a(A), .b(16'h1), .out(adder_1_out), .cout(Cout));  // open: cin
  Multiplier #(.width(16)) multiplier_1 (.a(A), .b(B), .out(multiplier_1_out));  // open: cin, cout
  Divider #(.width(16)) divider_1 (.a(A), .b(B), .out(divider_1_out));  // open: upper, rem
  Subtractor #(.width(16)) subtractor_1 (.a(A), .b(B), .out(subtractor_1_out));  // open: bin, bout
  Adder #(.width(16)) adder_2 (.a(A), .b(B), .out(adder_2_out));  // open: cin, cout
  assign xor_1_out = A ^ B;  // XOR_Gate xor_1, 16 bits wide
  Multiplexer #(.select(3), .width(16), .enable("false")) multiplexer_1 (
    .in1(A), .in2(adder_1_out), .in3(multiplier_1_out), .in4(subtractor_1_out), .in5(divider_1_out),
    .in6(adder_2_out), .in7(xor_1_out), .out(out), .sel(in_2));  // open: in0
endmodule
